// Logisim project CSC-FinalProject.circ as structural Verilog: 16 circuits, main circuit main
module main (
  input  Clock
);

  wire and_1_out, control_unit_1_alusrc, control_unit_1_branch, control_unit_1_jump, control_unit_1_memtoreg,
       control_unit_1_memwrite, control_unit_1_regdst, control_unit_1_regwrite, n8_bit_alu_1_zero;
  wire [2:0] control_unit_1_alu_control, multiplexer_2_out;
  wire [7:0] bit_extender_3_out, multiplexer_3_out, multiplexer_5_out, n8_bit_alu_1_aluout, ram_2_data,
       register_file_1_read_data_1, register_file_1_read_data_2;
  wire [16:0] adder_1_out;
  wire [20:0] bit_extender_1_out, bit_extender_2_out, multiplexer_1_out, multiplexer_4_out, ram_1_data,
       register_1_q;

  Register #(.width(21)) register_1 (.D(multiplexer_1_out), .en(1'b1), .Q(register_1_q), .clk(Clock));  // open: clr
  Multiplexer #(.width(21), .enable("false")) multiplexer_1 (
    .in0(multiplexer_4_out), .in1(bit_extender_2_out), .out(multiplexer_1_out), .sel(control_unit_1_jump));
  Adder #(.width(21)) adder_1 (
    .a(21'h1), .b(register_1_q), .out({bit_extender_2_out[20:17], adder_1_out}));  // open: cin, cout
  RAM #(.addrWidth(21), .dataWidth(21)) ram_1 (.addr(register_1_q), .data(ram_1_data));  // open: sel, clk, ld, clr
  assign bit_extender_1_out = {{15{ram_1_data[5]}}, ram_1_data[5:0]};  // Bit_Extender bit_extender_1
  assign bit_extender_2_out[16:0] = {{2{ram_1_data[14]}}, ram_1_data[14:0]};  // Bit_Extender bit_extender_2
  Control_Unit control_unit_1 (
    .OPcode(ram_1_data[20:15]), .funct(ram_1_data[5:0]), .MemtoReg(control_unit_1_memtoreg),
    .MemWrite(control_unit_1_memwrite), .Branch(control_unit_1_branch), .ALUSrc(control_unit_1_alusrc),
    .RegDst(control_unit_1_regdst), .RegWrite(control_unit_1_regwrite), .Jump(control_unit_1_jump),
    .ALU_control(control_unit_1_alu_control));
  assign bit_extender_3_out = {{2{ram_1_data[5]}}, ram_1_data[5:0]};  // Bit_Extender bit_extender_3
  Multiplexer #(.width(3), .enable("false")) multiplexer_2 (
    .in0(ram_1_data[11:9]), .in1(ram_1_data[8:6]), .out(multiplexer_2_out), .sel(control_unit_1_regdst));
  Register_File register_file_1 (
    .Data_in(multiplexer_5_out), .Write_Enable(control_unit_1_regwrite), .Clock(Clock),
    .Write_Addr(multiplexer_2_out), .Read_Addr_1(ram_1_data[14:12]), .Read_Addr_2(ram_1_data[11:9]),
    .Read_Data_1(register_file_1_read_data_1), .Read_Data_2(register_file_1_read_data_2));
  _8_bit_ALU u_8_bit_alu_1 (
    .A(register_file_1_read_data_1), .B(multiplexer_3_out), .ALU_control(control_unit_1_alu_control),
    .Zero(n8_bit_alu_1_zero), .ALUout(n8_bit_alu_1_aluout));
  Multiplexer #(.width(8), .enable("false")) multiplexer_3 (
    .in0(register_file_1_read_data_2), .in1(bit_extender_3_out), .out(multiplexer_3_out),
    .sel(control_unit_1_alusrc));
  Multiplexer #(.width(21), .enable("false")) multiplexer_4 (
    .in0({bit_extender_2_out[20:17], adder_1_out}), .in1(bit_extender_1_out), .out(multiplexer_4_out),
    .sel(and_1_out));
  and and_1 (and_1_out, n8_bit_alu_1_zero, control_unit_1_branch);
  RAM #(.bus("separate")) ram_2 (
    .addr(n8_bit_alu_1_aluout), .din(register_file_1_read_data_2), .data(ram_2_data),
    .str(control_unit_1_memwrite), .clk(Clock));  // open: sel, ld, clr
  Multiplexer #(.width(8), .enable("false")) multiplexer_5 (
    .in0(n8_bit_alu_1_aluout), .in1(ram_2_data), .out(multiplexer_5_out), .sel(control_unit_1_memtoreg));

  // Notes on the sheet:
  //   PC+4
  //   Jump
  //   IM
  //   WriteAddr
  //   Imm
  //   OPcode
  //   RA2
  //   Tag
  //   4 MSB of PC + 4
  //   funct
  //   RA1
  //   RegWrite
  //   RegDst
  //   ALUcontrol
  //   PC+4
  //   ALUsrc
  //   PC+4
  //   Zero
  //   PCSrc
  //   Jump
  //   Branch
  //   DM
  //   MemtoReg
  //   MemWrite
endmodule

// ALU
module _8_bit_ALU (
  input  [7:0] A,
  input  [7:0] B,
  input  [2:0] ALU_control,
  output Zero,
  output [7:0] ALUout
);

  wire and_1_out;
  wire [6:0] adder_1_out;
  wire [7:0] and_2_out, multiplexer_1_out, not_1_out, or_1_out;
  wire [7:7] adder_1_out_2;

  assign not_1_out = ~B;  // NOT_Gate not_1, 8 bits wide
  Multiplexer #(.width(8), .enable("false")) multiplexer_1 (
    .in0(B), .in1(not_1_out), .out(multiplexer_1_out), .sel(and_1_out));
  and and_1 (and_1_out, ALU_control[1], ALU_control[2]);
  assign and_2_out = A & B;  // AND_Gate and_2, 8 bits wide
  assign or_1_out = A | B;  // OR_Gate or_1, 8 bits wide
  Adder adder_1 (.a(A), .b(multiplexer_1_out), .out({adder_1_out_2[7], adder_1_out}), .cin(and_1_out));  // open: cout
  Multiplexer #(.select(3), .width(8), .enable("false")) multiplexer_2 (
    .in0(and_2_out), .in1(or_1_out), .in2({adder_1_out_2[7], adder_1_out}),
    .in6({adder_1_out_2[7], adder_1_out}), .in7({{7{1'b0}}, adder_1_out_2[7]}), .out(ALUout),
    .sel(ALU_control));  // open: in3, in4, in5
  Comparator comparator_1 (.a({8{1'b0}}), .b(ALUout), .eq(Zero));  // open: gt, lt

  // Notes on the sheet:
  //   8-bit ALU
  //   000 and
  //   001 or
  //   010 add
  //   110 sub
  //   111 slt
  //   sub/slt
  //   MSB == 1
  //   Less
  //   slt
  //   Equals
endmodule

module Equals (
  input  [5:0] Input_1,
  input  [5:0] Input_2,
  output Result
);

  wire xnor_1_out, xnor_2_out, xnor_3_out, xnor_4_out, xnor_5_out, xnor_6_out;

  xnor xnor_1 (xnor_1_out, Input_1[5], Input_2[5]);
  xnor xnor_2 (xnor_2_out, Input_1[4], Input_2[4]);
  xnor xnor_3 (xnor_3_out, Input_1[3], Input_2[3]);
  xnor xnor_4 (xnor_4_out, Input_1[2], Input_2[2]);
  xnor xnor_5 (xnor_5_out, Input_1[1], Input_2[1]);
  xnor xnor_6 (xnor_6_out, Input_1[0], Input_2[0]);
  and and_1 (Result, xnor_1_out, xnor_2_out, xnor_3_out, xnor_4_out, xnor_5_out, xnor_6_out);
endmodule

module NotEquals (
  input  [5:0] Input_1,
  input  [5:0] Input_2,
  output Result
);

  wire equals_1_result;

  Equals equals_1 (.Input_1(Input_1), .Input_2(Input_2), .Result(equals_1_result));
  not not_1 (Result, equals_1_result);
endmodule

module RegDst (
  input  [5:0] OPcode,
  output RegDst
);

  Equals equals_1 (.Input_1(OPcode), .Input_2({6{1'b0}}), .Result(RegDst));
endmodule

module ALUSrc (
  input  [5:0] OPcode,
  output ALUSrc
);

  wire equals_1_result, equals_2_result, equals_3_result;

  Equals equals_1 (.Input_1(OPcode), .Input_2(6'b100011), .Result(equals_1_result));
  Equals equals_2 (.Input_1(OPcode), .Input_2(6'b101011), .Result(equals_2_result));
  Equals equals_3 (.Input_1(OPcode), .Input_2(6'b001000), .Result(equals_3_result));
  or or_1 (ALUSrc, equals_1_result, equals_2_result, equals_3_result);

  // Notes on the sheet:
  //   100011
  //   101011
  //   001000
endmodule

module MemtoReg (
  input  [5:0] OPcode,
  output MemtoReg
);

  Equals equals_1 (.Input_1(OPcode), .Input_2(6'b100011), .Result(MemtoReg));

  // Notes on the sheet:
  //   100011
endmodule

module MemWrite (
  input  [5:0] OPcode,
  output MemWrite
);

  Equals equals_1 (.Input_1(OPcode), .Input_2(6'b101011), .Result(MemWrite));

  // Notes on the sheet:
  //   101011
endmodule

module RegWrite (
  input  [5:0] OPcode,
  output RegWrite
);

  wire equals_1_result, equals_2_result, equals_3_result;

  Equals equals_1 (.Input_1(OPcode), .Input_2({6{1'b0}}), .Result(equals_1_result));
  Equals equals_2 (.Input_1(OPcode), .Input_2(6'b100011), .Result(equals_2_result));
  Equals equals_3 (.Input_1(OPcode), .Input_2(6'b001000), .Result(equals_3_result));
  or or_1 (RegWrite, equals_1_result, equals_2_result, equals_3_result);

  // Notes on the sheet:
  //   000000
  //   100011
  //   001000
endmodule

module ALUop (
  input  [5:0] OPcode,
  output [1:0] out_2
);

  Equals equals_1 (.Input_1(OPcode), .Input_2({6{1'b0}}), .Result(out_2[1]));
  Equals equals_2 (.Input_1(OPcode), .Input_2(6'b000100), .Result(out_2[0]));

  // Notes on the sheet:
  //   000100
  //   000000
  //   ALUop[0]
  //   ALUop[1]
endmodule

module Jump (
  input  [5:0] OPcode,
  output Jump
);

  Equals equals_1 (.Input_1(6'b000010), .Input_2(OPcode), .Result(Jump));

  // Notes on the sheet:
  //   000010
endmodule

module Branch (
  input  [5:0] OPcode,
  output Branch
);

  Equals equals_1 (.Input_1(OPcode), .Input_2(6'b000100), .Result(Branch));

  // Notes on the sheet:
  //   000100
endmodule

module MainDecoder (
  input  [5:0] OPcode,
  output MemtoReg,
  output MemWrite,
  output Branch,
  output [1:0] ALUop,
  output ALUSrc,
  output RegDst,
  output RegWrite,
  output Jump
);

  MemtoReg u_MemtoReg (.OPcode(OPcode), .MemtoReg(MemtoReg));
  MemWrite u_MemWrite (.OPcode(OPcode), .MemWrite(MemWrite));
  Branch u_Branch (.OPcode(OPcode), .Branch(Branch));
  ALUop u_ALUop (.OPcode(OPcode), .out_2(ALUop));
  ALUSrc u_ALUSrc (.OPcode(OPcode), .ALUSrc(ALUSrc));
  RegDst u_RegDst (.OPcode(OPcode), .RegDst(RegDst));
  RegWrite u_RegWrite (.OPcode(OPcode), .RegWrite(RegWrite));
  Jump u_Jump (.OPcode(OPcode), .Jump(Jump));
endmodule

module ALUdecoder (
  input  [1:0] ALUop,
  input  [5:0] funct,
  output [2:0] ALUcontrol
);

  wire and_1_out, or_1_out;

  or or_1 (or_1_out, funct[3], funct[0]);
  and and_1 (and_1_out, ALUop[1], funct[1]);
  and and_2 (ALUcontrol[0], ALUop[1], or_1_out);
  or or_2 (ALUcontrol[2], ALUop[0], and_1_out);
  or or_3 (ALUcontrol[1], ~ALUop[1], ~funct[2]);  // OR_Gate
endmodule

module Control_Unit (
  input  [5:0] OPcode,
  input  [5:0] funct,
  output MemtoReg,
  output MemWrite,
  output Branch,
  output ALUSrc,
  output RegDst,
  output RegWrite,
  output Jump,
  output [2:0] ALU_control
);

  wire [1:0] Main_decoder_aluop;

  MainDecoder Main_decoder (
    .OPcode(OPcode), .MemtoReg(MemtoReg), .MemWrite(MemWrite), .Branch(Branch), .ALUop(Main_decoder_aluop),
    .ALUSrc(ALUSrc), .RegDst(RegDst), .RegWrite(RegWrite), .Jump(Jump));
  ALUdecoder aludecoder_1 (.ALUop(Main_decoder_aluop), .funct(funct), .ALUcontrol(ALU_control));
endmodule

// RF
module Register_File (
  input  [7:0] Data_in,
  input  [2:0] Read_Addr_1,
  input  Write_Enable,
  input  [2:0] Write_Addr,
  input  [2:0] Read_Addr_2,
  input  Clock,
  output [7:0] Read_Data_1,
  output [7:0] Read_Data_2
);

  wire demultiplexer_1_out0, demultiplexer_1_out1, demultiplexer_1_out2, demultiplexer_1_out3,
       demultiplexer_1_out4, demultiplexer_1_out5, demultiplexer_1_out6, demultiplexer_1_out7;
  wire [7:0] register_1_q, register_2_q, register_3_q, register_4_q, register_5_q, register_6_q,
       register_7_q, register_8_q;

  Demultiplexer #(.select(3), .enable("false")) demultiplexer_1 (
    .out0(demultiplexer_1_out0), .out1(demultiplexer_1_out1), .out2(demultiplexer_1_out2),
    .out3(demultiplexer_1_out3), .out4(demultiplexer_1_out4), .out5(demultiplexer_1_out5),
    .out6(demultiplexer_1_out6), .out7(demultiplexer_1_out7), .in(Write_Enable), .sel(Write_Addr));
  Register register_1 (.D(Data_in), .en(demultiplexer_1_out0), .Q(register_1_q), .clk(Clock));  // open: clr
  Register register_2 (.D(Data_in), .en(demultiplexer_1_out1), .Q(register_2_q), .clk(Clock));  // open: clr
  Register register_3 (.D(Data_in), .en(demultiplexer_1_out2), .Q(register_3_q), .clk(Clock));  // open: clr
  Register register_4 (.D(Data_in), .en(demultiplexer_1_out3), .Q(register_4_q), .clk(Clock));  // open: clr
  Register register_5 (.D(Data_in), .en(demultiplexer_1_out4), .Q(register_5_q), .clk(Clock));  // open: clr
  Register register_6 (.D(Data_in), .en(demultiplexer_1_out5), .Q(register_6_q), .clk(Clock));  // open: clr
  Register register_7 (.D(Data_in), .en(demultiplexer_1_out6), .Q(register_7_q), .clk(Clock));  // open: clr
  Register register_8 (.D(Data_in), .en(demultiplexer_1_out7), .Q(register_8_q), .clk(Clock));  // open: clr
  Multiplexer #(.select(3), .width(8), .enable("false")) multiplexer_1 (
    .in0(register_1_q), .in1(register_2_q), .in2(register_3_q), .in3(register_4_q), .in4(register_5_q),
    .in5(register_6_q), .in6(register_7_q), .in7(register_8_q), .out(Read_Data_1), .sel(Read_Addr_1));
  Multiplexer #(.select(3), .width(8), .enable("false")) multiplexer_2 (
    .in0(register_1_q), .in1(register_2_q), .in2(register_3_q), .in3(register_4_q), .in4(register_5_q),
    .in5(register_6_q), .in6(register_7_q), .in7(register_8_q), .out(Read_Data_2), .sel(Read_Addr_2));
endmodule
